// Logisim project EX1.circ as structural Verilog: 3 circuits, main circuit equation1
module equation1 (
  input  A,
  input  B,
  input  C,
  output X
);

  wire and_1_out, and_2_out, and_3_out, and_4_out, and_5_out, not_1_out, not_2_out, not_3_out, not_4_out;

  and and_1 (and_1_out, A, B);
  and and_2 (and_2_out, A, not_1_out);
  not not_1 (not_1_out, B);
  not not_2 (not_2_out, A);
  and and_3 (and_3_out, not_2_out, not_3_out);
  not not_3 (not_3_out, C);
  and and_4 (and_4_out, and_1_out, C);
  and and_5 (and_5_out, and_2_out, not_4_out);
  not not_4 (not_4_out, and_3_out);
  or or_1 (X, and_4_out, and_5_out);

  // Notes on the sheet:
  //   10 portas logicas
endmodule

module equation2 (
  input  A,
  input  B,
  input  C,
  output X
);

  wire and_1_out, and_2_out, not_1_out;

  not not_1 (not_1_out, B);
  and and_1 (and_1_out, A, C);
  and and_2 (and_2_out, A, not_1_out);
  or or_1 (X, and_1_out, and_2_out);

  // Notes on the sheet:
  //   4 portas logicas
endmodule

module equation2_reduced (
  input  A,
  input  B,
  input  C,
  output X
);

  wire not_1_out, or_1_out;

  not not_1 (not_1_out, B);
  or or_1 (or_1_out, not_1_out, C);
  and and_1 (X, A, or_1_out);

  // Notes on the sheet:
  //   3 portas logicas
endmodule
