// Logisim project EX2_1.circ as structural Verilog: 5 circuits, main circuit detector_erro
module detector_erro (
  input  A3,
  input  A2,
  input  A1,
  input  A0,
  output E
);

  wire xor_1_out, xor_2_out, xor_3_out;

  xor xor_1 (xor_1_out, A3, A2);
  xor xor_2 (xor_2_out, xor_1_out, A1);
  xor xor_3 (xor_3_out, xor_2_out, A0);
  xor xor_4 (E, xor_3_out, xor_3_out);
endmodule

module detector_erro_andornot (
  input  A3,
  input  A2,
  input  A1,
  input  A0,
  output E
);

  wire and_1_out, and_2_out, and_3_out, and_4_out, and_5_out, and_6_out, and_7_out, and_8_out, not_1_out,
       not_2_out, not_3_out, not_4_out, not_5_out, not_6_out, not_7_out, not_8_out, or_1_out, or_2_out,
       or_3_out;

  not not_1 (not_1_out, A3);
  not not_2 (not_2_out, A2);
  and and_1 (and_1_out, A2, not_1_out);
  and and_2 (and_2_out, not_2_out, A3);
  or or_1 (or_1_out, and_1_out, and_2_out);
  and and_3 (and_3_out, or_1_out, not_3_out);
  not not_3 (not_3_out, A1);
  not not_4 (not_4_out, or_1_out);
  and and_4 (and_4_out, not_4_out, A1);
  or or_2 (or_2_out, and_3_out, and_4_out);
  not not_5 (not_5_out, A0);
  not not_6 (not_6_out, or_2_out);
  and and_5 (and_5_out, or_2_out, not_5_out);
  and and_6 (and_6_out, not_6_out, A0);
  or or_3 (or_3_out, and_5_out, and_6_out);
  and and_7 (and_7_out, or_3_out, not_7_out);
  not not_7 (not_7_out, or_3_out);
  not not_8 (not_8_out, or_3_out);
  and and_8 (and_8_out, not_8_out, or_3_out);
  or or_4 (E, and_7_out, and_8_out);
endmodule

module xor_CI (
  input  A,
  input  B,
  output X
);

  wire and_1_out, and_2_out, n7404_1_pin6, n7404_1_pin8, n7408_1_pin3, n7408_1_pin11, not_1_out, not_2_out;

  and and_1 (and_1_out, A, not_1_out);
  not not_1 (not_1_out, B);
  not not_2 (not_2_out, A);
  and and_2 (and_2_out, not_2_out, B);
  // OR_Gate or_1 has open pins: in0=and_1_out, in1=and_2_out, out=open
  _7404 u_7404_1 (
    .pin5(A), .pin6(n7404_1_pin6), .pin9(B), .pin8(n7404_1_pin8));  // open: pin1, pin2, pin3, pin4, pin13, pin12, pin11, pin10
  _7408 u_7408_1 (
    .pin1(n7404_1_pin6), .pin2(B), .pin3(n7408_1_pin3), .pin13(n7404_1_pin8), .pin12(A), .pin11(n7408_1_pin11));  // open: pin4, pin5, pin6, pin10, pin9, pin8
  _7432 u_7432_1 (
    .pin13(n7408_1_pin3), .pin12(n7408_1_pin11), .pin11(X));  // open: pin1, pin2, pin3, pin4, pin5, pin6, pin10, pin9, pin8
endmodule

module detector_erro_CI_abstrato (
  input  A3,
  input  A2,
  input  A1,
  input  A0,
  output E
);

  wire xor_ci_1_x, xor_ci_2_x, xor_ci_3_x;

  xor_CI xor_ci_1 (.A(A2), .B(A3), .X(xor_ci_1_x));
  xor_CI xor_ci_2 (.A(xor_ci_1_x), .B(A1), .X(xor_ci_2_x));
  xor_CI xor_ci_3 (.A(xor_ci_2_x), .B(A0), .X(xor_ci_3_x));
  xor_CI xor_ci_4 (.A(xor_ci_3_x), .B(xor_ci_3_x), .X(E));
endmodule

module detector_erro_CI_explicito (
  input  A3,
  input  A2,
  input  A1,
  input  A0,
  output E
);

  wire n7404_1_pin6, n7404_1_pin8, n7404_2_pin5, n7404_2_pin6, n7404_2_pin8, n7404_3_pin5, n7404_3_pin6,
       n7404_3_pin8, n7404_4_pin5, n7404_4_pin6, n7404_4_pin8, n7408_1_pin3, n7408_1_pin11, n7408_2_pin3,
       n7408_2_pin11, n7408_3_pin3, n7408_3_pin11, n7408_4_pin3, n7408_4_pin11;

  _7404 u_7404_1 (
    .pin5(A2), .pin6(n7404_1_pin6), .pin9(A3), .pin8(n7404_1_pin8));  // open: pin1, pin2, pin3, pin4, pin13, pin12, pin11, pin10
  _7404 u_7404_2 (
    .pin5(n7404_2_pin5), .pin6(n7404_2_pin6), .pin9(A1), .pin8(n7404_2_pin8));  // open: pin1, pin2, pin3, pin4, pin13, pin12, pin11, pin10
  _7404 u_7404_3 (
    .pin5(n7404_3_pin5), .pin6(n7404_3_pin6), .pin9(A0), .pin8(n7404_3_pin8));  // open: pin1, pin2, pin3, pin4, pin13, pin12, pin11, pin10
  _7404 u_7404_4 (
    .pin5(n7404_4_pin5), .pin6(n7404_4_pin6), .pin9(n7404_4_pin5), .pin8(n7404_4_pin8));  // open: pin1, pin2, pin3, pin4, pin13, pin12, pin11, pin10
  _7408 u_7408_1 (
    .pin1(n7404_1_pin6), .pin2(A3), .pin3(n7408_1_pin3), .pin13(n7404_1_pin8), .pin12(A2),
    .pin11(n7408_1_pin11));  // open: pin4, pin5, pin6, pin10, pin9, pin8
  _7408 u_7408_2 (
    .pin1(n7404_2_pin6), .pin2(A1), .pin3(n7408_2_pin3), .pin13(n7404_2_pin8), .pin12(n7404_2_pin5),
    .pin11(n7408_2_pin11));  // open: pin4, pin5, pin6, pin10, pin9, pin8
  _7408 u_7408_3 (
    .pin1(n7404_3_pin6), .pin2(A0), .pin3(n7408_3_pin3), .pin13(n7404_3_pin8), .pin12(n7404_3_pin5),
    .pin11(n7408_3_pin11));  // open: pin4, pin5, pin6, pin10, pin9, pin8
  _7408 u_7408_4 (
    .pin1(n7404_4_pin6), .pin2(n7404_4_pin5), .pin3(n7408_4_pin3), .pin13(n7404_4_pin8),
    .pin12(n7404_4_pin5), .pin11(n7408_4_pin11));  // open: pin4, pin5, pin6, pin10, pin9, pin8
  _7432 u_7432_1 (
    .pin13(n7408_1_pin3), .pin12(n7408_1_pin11), .pin11(n7404_2_pin5));  // open: pin1, pin2, pin3, pin4, pin5, pin6, pin10, pin9, pin8
  _7432 u_7432_2 (
    .pin13(n7408_2_pin3), .pin12(n7408_2_pin11), .pin11(n7404_3_pin5));  // open: pin1, pin2, pin3, pin4, pin5, pin6, pin10, pin9, pin8
  _7432 u_7432_3 (
    .pin13(n7408_3_pin3), .pin12(n7408_3_pin11), .pin11(n7404_4_pin5));  // open: pin1, pin2, pin3, pin4, pin5, pin6, pin10, pin9, pin8
  _7432 u_7432_4 (
    .pin13(n7408_4_pin3), .pin12(n7408_4_pin11), .pin11(E));  // open: pin1, pin2, pin3, pin4, pin5, pin6, pin10, pin9, pin8
endmodule
