// Logisim project EX2_2.circ as structural Verilog: 3 circuits, main circuit EX2_2
module EX2_2 (
  input  A2,
  input  A1,
  input  A0,
  output X
);

  wire not_1_out, not_2_out, not_3_out, not_4_out, not_5_out, or_1_out, or_2_out, or_3_out;

  not not_1 (not_1_out, A1);
  not not_2 (not_2_out, A2);
  not not_3 (not_3_out, A0);
  not not_4 (not_4_out, A2);
  not not_5 (not_5_out, A1);
  or or_1 (or_1_out, A2, not_1_out, A0);
  or or_2 (or_2_out, not_2_out, A1, not_3_out);
  or or_3 (or_3_out, not_4_out, not_5_out, A0);
  and and_1 (X, or_1_out, or_2_out, or_3_out);
endmodule

module EX2_2_2GATE (
  input  A2,
  input  A1,
  input  A0,
  output X
);

  wire and_1_out, not_1_out, not_2_out, not_3_out, or_1_out, or_2_out, or_3_out, or_4_out, or_5_out, or_6_out;

  not not_1 (not_1_out, A2);
  not not_2 (not_2_out, A1);
  not not_3 (not_3_out, A0);
  or or_1 (or_1_out, A2, not_2_out);
  or or_2 (or_2_out, not_1_out, A1);
  or or_3 (or_3_out, or_1_out, A0);
  and and_1 (and_1_out, or_3_out, or_4_out);
  or or_4 (or_4_out, or_2_out, not_3_out);
  or or_5 (or_5_out, not_1_out, not_2_out);
  or or_6 (or_6_out, or_5_out, A0);
  and and_2 (X, and_1_out, or_6_out);
endmodule

module EX2_2_CI (
  input  A2,
  input  A1,
  input  A0,
  output out_4
);

  wire n7404_1_pin8, n7404_1_pin10, n7404_1_pin12, n7408_1_pin11, n7432_1_pin1, n7432_1_pin3, n7432_1_pin4,
       n7432_1_pin6, n7432_2_pin3, n7432_2_pin8;

  _7404 u_7404_1 (
    .pin13(A2), .pin12(n7404_1_pin12), .pin11(A1), .pin10(n7404_1_pin10), .pin9(A0), .pin8(n7404_1_pin8));  // open: pin1, pin2, pin3, pin4, pin5, pin6
  _7432 u_7432_1 (
    .pin1(n7432_1_pin1), .pin2(A0), .pin3(n7432_1_pin3), .pin4(n7432_1_pin4), .pin5(n7404_1_pin8),
    .pin6(n7432_1_pin6), .pin13(A2), .pin12(n7404_1_pin10), .pin11(n7432_1_pin1), .pin10(n7404_1_pin12),
    .pin9(A1), .pin8(n7432_1_pin4));
  _7432 u_7432_2 (
    .pin1(n7404_1_pin10), .pin2(n7404_1_pin12), .pin3(n7432_2_pin3), .pin10(A0), .pin9(n7432_2_pin3),
    .pin8(n7432_2_pin8));  // open: pin4, pin5, pin6, pin13, pin12, pin11
  _7408 u_7408_1 (
    .pin13(n7432_1_pin3), .pin12(n7432_1_pin6), .pin11(n7408_1_pin11), .pin10(n7408_1_pin11),
    .pin9(n7432_2_pin8), .pin8(out_4));  // open: pin1, pin2, pin3, pin4, pin5, pin6
endmodule
