// Logisim project EX3.circ as structural Verilog: 3 circuits, main circuit SOP
module SOP (
  input  A3,
  input  A2,
  input  A1,
  input  A0,
  output X
);

  wire and_1_out, and_2_out, and_3_out;

  and and_1 (and_1_out, A2, A1);
  and and_2 (and_2_out, A3, A0);
  and and_3 (and_3_out, A3, A1);
  or or_1 (X, and_1_out, and_2_out, and_3_out);

  // Notes on the sheet:
  //   X = A3A1 + A3A0 + A2A1
  //   A2A1
  //   A3A0
  //   A3A1
endmodule

module POS (
  input  A3,
  input  A2,
  input  A1,
  input  A0,
  output X
);

  wire or_1_out, or_2_out, or_3_out;

  or or_1 (or_1_out, A3, A2);
  or or_2 (or_2_out, A3, A1);
  or or_3 (or_3_out, A1, A0);
  and and_1 (X, or_1_out, or_2_out, or_3_out);

  // Notes on the sheet:
  //   X = (A1 + A0)(A3 + A2)(A3 + A1)
endmodule

module VERIFY (
  output [3:0] A3A2A1A0,
  output X_SOP,
  output X_POS
);

  wire clock_1_out;

  Clock clock_1 (.out(clock_1_out));
  Counter #(.max('hf), .width(4)) counter_1 (.Q(A3A2A1A0), .clk(clock_1_out));  // open: load, D, count, carry, up, clr
  SOP sop_1 (.A3(A3A2A1A0[3]), .A2(A3A2A1A0[2]), .A1(A3A2A1A0[1]), .A0(A3A2A1A0[0]), .X(X_SOP));
  POS pos_1 (.A3(A3A2A1A0[3]), .A2(A3A2A1A0[2]), .A1(A3A2A1A0[1]), .A0(A3A2A1A0[0]), .X(X_POS));
endmodule
