// Logisim project EX4.circ as structural Verilog: 3 circuits, main circuit main
module main (
  input  A5,
  input  A4,
  input  A3,
  input  A2,
  input  A1,
  input  A0,
  output X
);

  wire and_1_out, and_2_out, and_3_out, and_4_out, and_5_out, and_6_out, and_7_out, and_8_out, and_9_out,
       not_1_out, not_2_out, not_3_out, not_4_out, not_5_out, not_6_out;

  not not_1 (not_1_out, A5);
  not not_2 (not_2_out, A4);
  not not_3 (not_3_out, A3);
  not not_4 (not_4_out, A2);
  not not_5 (not_5_out, A1);
  not not_6 (not_6_out, A0);
  and and_1 (and_1_out, not_1_out, not_2_out, not_4_out, not_5_out);
  and and_2 (and_2_out, not_1_out, not_2_out, not_4_out, not_6_out);
  and and_3 (and_3_out, not_1_out, not_2_out, A2, A1, A0);
  and and_4 (and_4_out, not_1_out, not_3_out, not_4_out);
  and and_5 (and_5_out, A5, A4, A3);
  and and_6 (and_6_out, not_1_out, not_3_out, not_5_out);
  and and_7 (and_7_out, not_1_out, not_3_out, not_6_out);
  and and_8 (and_8_out, A5, A4, A2, A0);
  and and_9 (and_9_out, A5, A4, A2, A1);
  or or_1 (X, and_1_out, and_2_out, and_3_out, and_4_out, and_5_out, and_6_out, and_7_out, and_8_out, and_9_out);
endmodule

module SOP (
  input  A5,
  input  A4,
  input  A3,
  input  A2,
  input  A1,
  input  A0,
  output X
);

  wire and_1_out, and_2_out, and_3_out, and_4_out, and_5_out, and_6_out, and_7_out, and_8_out, and_9_out,
       not_1_out, not_2_out, not_3_out, not_4_out, not_5_out, not_6_out;

  not not_1 (not_1_out, A5);
  not not_2 (not_2_out, A4);
  not not_3 (not_3_out, A3);
  not not_4 (not_4_out, A2);
  not not_5 (not_5_out, A1);
  not not_6 (not_6_out, A0);
  and and_1 (and_1_out, not_1_out, not_2_out, not_4_out, not_5_out);
  and and_2 (and_2_out, not_1_out, not_2_out, not_4_out, not_6_out);
  and and_3 (and_3_out, not_1_out, not_2_out, A2, A1, A0);
  and and_4 (and_4_out, not_1_out, not_3_out, not_4_out);
  and and_5 (and_5_out, A5, A4, A3);
  and and_6 (and_6_out, not_1_out, not_3_out, not_5_out);
  and and_7 (and_7_out, not_1_out, not_3_out, not_6_out);
  and and_8 (and_8_out, A5, A4, A2, A0);
  and and_9 (and_9_out, A5, A4, A2, A1);
  or or_1 (X, and_1_out, and_2_out, and_3_out, and_4_out, and_5_out, and_6_out, and_7_out, and_8_out, and_9_out);
endmodule

module POS (
  input  A5,
  input  A4,
  input  A3,
  input  A2,
  input  A1,
  input  A0,
  output X
);

  wire not_1_out, not_2_out, not_3_out, not_4_out, not_5_out, not_6_out, or_1_out, or_2_out, or_3_out,
       or_4_out, or_5_out, or_6_out, or_7_out, or_8_out;

  not not_1 (not_1_out, A5);
  not not_2 (not_2_out, A4);
  not not_3 (not_3_out, A3);
  not not_4 (not_4_out, A2);
  not not_5 (not_5_out, A1);
  not not_6 (not_6_out, A0);
  or or_1 (or_1_out, A5, not_2_out, not_4_out, not_5_out, not_6_out);
  or or_2 (or_2_out, A5, not_2_out, not_3_out);
  or or_3 (or_3_out, not_1_out, A4);
  or or_4 (or_4_out, not_1_out, A3, A2);
  or or_5 (or_5_out, not_1_out, A3, A1, A0);
  or or_6 (or_6_out, A5, not_3_out, A2, not_5_out, not_6_out);
  or or_7 (or_7_out, A5, not_3_out, not_4_out, A1);
  or or_8 (or_8_out, A4, not_3_out, not_4_out, A0);
  and and_1 (X, or_1_out, or_2_out, or_3_out, or_4_out, or_5_out, or_6_out, or_7_out, or_8_out);
endmodule
