// Logisim project EX1.circ as structural Verilog: 2 circuits, main circuit latch_nand2
module latch_nand (
  input  S,
  input  R,
  output nQ,
  output Q
);

  nand nand_1 (nQ, S, Q);
  nand nand_2 (Q, nQ, R);
endmodule

module latch_nand2 (
  input  S,
  input  R,
  output nQ,
  output nQ_1,
  output Q,
  output Q_1
);

  nand nand_1 (nQ, S, Q);
  nand nand_2 (Q, nQ, R);
  nand nand_3 (nQ_1, Q, Q_1);
  nand nand_4 (Q_1, nQ_1, nQ);
endmodule
