// Logisim project EX2.circ as structural Verilog: 2 circuits, main circuit memory4bits
module memory4bits (
  input  D3,
  input  D2,
  input  D1,
  input  D0,
  input  EN,
  output S3,
  output S2,
  output S1,
  output S0
);

  wire and_1_out, clock_1_out;

  Clock clock_1 (.out(clock_1_out));
  and and_1 (and_1_out, EN, clock_1_out);
  D_Flip_Flop d_ff_1 (.D(D3), .clk(and_1_out), .Q(S3));  // open: Qn, preset, reset
  D_Flip_Flop d_ff_2 (.D(D2), .clk(and_1_out), .Q(S2));  // open: Qn, preset, reset
  D_Flip_Flop d_ff_3 (.D(D1), .clk(and_1_out), .Q(S1));  // open: Qn, preset, reset
  D_Flip_Flop d_ff_4 (.D(D0), .clk(and_1_out), .Q(S0));  // open: Qn, preset, reset
endmodule

module EX2 (
  input  [3:0] Address,
  input  D3,
  input  D2,
  input  D1,
  input  D0
);

  wire and_1_out, and_2_out, and_3_out, and_4_out, and_5_out, and_6_out, and_7_out, and_8_out, and_9_out,
       and_10_out, and_11_out, and_12_out, and_13_out, and_14_out, and_15_out, and_16_out, clock_1_out,
       decoder_1_out0, decoder_1_out1, decoder_1_out2, decoder_1_out3, decoder_1_out4, decoder_1_out5,
       decoder_1_out6, decoder_1_out7, decoder_1_out8, decoder_1_out9, decoder_1_out10, decoder_1_out11,
       decoder_1_out12, decoder_1_out13, decoder_1_out14, decoder_1_out15;

  Decoder #(.enable("false"), .select(4)) decoder_1 (
    .out0(decoder_1_out0), .out1(decoder_1_out1), .out2(decoder_1_out2), .out3(decoder_1_out3),
    .out4(decoder_1_out4), .out5(decoder_1_out5), .out6(decoder_1_out6), .out7(decoder_1_out7),
    .out8(decoder_1_out8), .out9(decoder_1_out9), .out10(decoder_1_out10), .out11(decoder_1_out11),
    .out12(decoder_1_out12), .out13(decoder_1_out13), .out14(decoder_1_out14), .out15(decoder_1_out15),
    .sel(Address));
  Clock clock_1 (.out(clock_1_out));
  and and_1 (and_1_out, decoder_1_out0, clock_1_out);
  and and_2 (and_2_out, decoder_1_out4, clock_1_out);
  and and_3 (and_3_out, decoder_1_out8, clock_1_out);
  and and_4 (and_4_out, decoder_1_out12, clock_1_out);
  memory4bits memory4bits_1 (.EN(and_1_out), .D3(D3), .D2(D2), .D1(D1), .D0(D0));  // open: S3, S2, S1, S0
  memory4bits memory4bits_2 (.EN(and_2_out), .D3(D3), .D2(D2), .D1(D1), .D0(D0));  // open: S3, S2, S1, S0
  memory4bits memory4bits_3 (.EN(and_3_out), .D3(D3), .D2(D2), .D1(D1), .D0(D0));  // open: S3, S2, S1, S0
  memory4bits memory4bits_4 (.EN(and_4_out), .D3(D3), .D2(D2), .D1(D1), .D0(D0));  // open: S3, S2, S1, S0
  and and_5 (and_5_out, decoder_1_out1, clock_1_out);
  and and_6 (and_6_out, decoder_1_out5, clock_1_out);
  and and_7 (and_7_out, decoder_1_out9, clock_1_out);
  and and_8 (and_8_out, decoder_1_out13, clock_1_out);
  memory4bits memory4bits_5 (.EN(and_5_out), .D3(D3), .D2(D2), .D1(D1), .D0(D0));  // open: S3, S2, S1, S0
  memory4bits memory4bits_6 (.EN(and_6_out), .D3(D3), .D2(D2), .D1(D1), .D0(D0));  // open: S3, S2, S1, S0
  memory4bits memory4bits_7 (.EN(and_7_out), .D3(D3), .D2(D2), .D1(D1), .D0(D0));  // open: S3, S2, S1, S0
  memory4bits memory4bits_8 (.EN(and_8_out), .D3(D3), .D2(D2), .D1(D1), .D0(D0));  // open: S3, S2, S1, S0
  and and_9 (and_9_out, decoder_1_out2, clock_1_out);
  and and_10 (and_10_out, decoder_1_out6, clock_1_out);
  and and_11 (and_11_out, decoder_1_out10, clock_1_out);
  and and_12 (and_12_out, decoder_1_out14, clock_1_out);
  memory4bits memory4bits_9 (.EN(and_9_out), .D3(D3), .D2(D2), .D1(D1), .D0(D0));  // open: S3, S2, S1, S0
  memory4bits memory4bits_10 (.EN(and_10_out), .D3(D3), .D2(D2), .D1(D1), .D0(D0));  // open: S3, S2, S1, S0
  memory4bits memory4bits_11 (.EN(and_11_out), .D3(D3), .D2(D2), .D1(D1), .D0(D0));  // open: S3, S2, S1, S0
  memory4bits memory4bits_12 (.EN(and_12_out), .D3(D3), .D2(D2), .D1(D1), .D0(D0));  // open: S3, S2, S1, S0
  and and_13 (and_13_out, decoder_1_out3, clock_1_out);
  and and_14 (and_14_out, decoder_1_out7, clock_1_out);
  and and_15 (and_15_out, decoder_1_out11, clock_1_out);
  and and_16 (and_16_out, decoder_1_out15, clock_1_out);
  memory4bits memory4bits_13 (.EN(and_13_out), .D3(D3), .D2(D2), .D1(D1), .D0(D0));  // open: S3, S2, S1, S0
  memory4bits memory4bits_14 (.EN(and_14_out), .D3(D3), .D2(D2), .D1(D1), .D0(D0));  // open: S3, S2, S1, S0
  memory4bits memory4bits_15 (.EN(and_15_out), .D3(D3), .D2(D2), .D1(D1), .D0(D0));  // open: S3, S2, S1, S0
  memory4bits memory4bits_16 (.EN(and_16_out), .D3(D3), .D2(D2), .D1(D1), .D0(D0));  // open: S3, S2, S1, S0

  // Notes on the sheet:
  //   CTRL+F9 = 1 tick
endmodule
