// Logisim project EX3.circ as structural Verilog: 2 circuits, main circuit shift_Register
module shift_Register (
  input  D,
  input  [1:0] Addr,
  input  EN
);

  wire and_1_out, and_2_out, and_3_out, and_4_out, clock_1_out, d_ff_1_q, d_ff_2_q, d_ff_3_q, d_ff_4_q,
       d_ff_5_q, d_ff_6_q, d_ff_7_q, d_ff_8_q, d_ff_9_q, d_ff_10_q, d_ff_11_q, d_ff_12_q, d_ff_13_q,
       d_ff_14_q, d_ff_15_q, d_ff_16_q, d_ff_17_q, d_ff_18_q, d_ff_19_q, d_ff_20_q, d_ff_21_q, d_ff_22_q,
       d_ff_23_q, d_ff_24_q, d_ff_25_q, d_ff_26_q, d_ff_27_q, d_ff_28_q, d_ff_29_q, d_ff_30_q, d_ff_31_q,
       d_ff_32_q, d_ff_33_q, d_ff_34_q, d_ff_35_q, d_ff_36_q, decoder_1_out0, decoder_1_out1, decoder_1_out2,
       decoder_1_out3;

  Clock clock_1 (.out(clock_1_out));
  Decoder #(.select(2)) decoder_1 (
    .out0(decoder_1_out0), .out1(decoder_1_out1), .out2(decoder_1_out2), .out3(decoder_1_out3), .sel(Addr),
    .en(EN));
  D_Flip_Flop d_ff_1 (.D(D), .clk(clock_1_out), .Q(d_ff_1_q));  // open: Qn, preset, reset
  D_Flip_Flop d_ff_2 (.D(d_ff_1_q), .clk(clock_1_out), .Q(d_ff_2_q));  // open: Qn, preset, reset
  D_Flip_Flop d_ff_3 (.D(d_ff_36_q), .clk(and_1_out), .Q(d_ff_3_q));  // open: Qn, preset, reset
  and and_1 (and_1_out, decoder_1_out0, clock_1_out);
  D_Flip_Flop d_ff_4 (.D(d_ff_36_q), .clk(and_2_out), .Q(d_ff_4_q));  // open: Qn, preset, reset
  and and_2 (and_2_out, decoder_1_out1, clock_1_out);
  D_Flip_Flop d_ff_5 (.D(d_ff_36_q), .clk(and_3_out), .Q(d_ff_5_q));  // open: Qn, preset, reset
  and and_3 (and_3_out, decoder_1_out2, clock_1_out);
  D_Flip_Flop d_ff_6 (.D(d_ff_36_q), .clk(and_4_out), .Q(d_ff_6_q));  // open: Qn, preset, reset
  and and_4 (and_4_out, decoder_1_out3, clock_1_out);
  D_Flip_Flop d_ff_7 (.D(d_ff_2_q), .clk(clock_1_out), .Q(d_ff_7_q));  // open: Qn, preset, reset
  D_Flip_Flop d_ff_8 (.D(d_ff_3_q), .clk(and_1_out), .Q(d_ff_8_q));  // open: Qn, preset, reset
  D_Flip_Flop d_ff_9 (.D(d_ff_4_q), .clk(and_2_out), .Q(d_ff_9_q));  // open: Qn, preset, reset
  D_Flip_Flop d_ff_10 (.D(d_ff_5_q), .clk(and_3_out), .Q(d_ff_10_q));  // open: Qn, preset, reset
  D_Flip_Flop d_ff_11 (.D(d_ff_6_q), .clk(and_4_out), .Q(d_ff_11_q));  // open: Qn, preset, reset
  D_Flip_Flop d_ff_12 (.D(d_ff_8_q), .clk(and_1_out), .Q(d_ff_12_q));  // open: Qn, preset, reset
  D_Flip_Flop d_ff_13 (.D(d_ff_9_q), .clk(and_2_out), .Q(d_ff_13_q));  // open: Qn, preset, reset
  D_Flip_Flop d_ff_14 (.D(d_ff_10_q), .clk(and_3_out), .Q(d_ff_14_q));  // open: Qn, preset, reset
  D_Flip_Flop d_ff_15 (.D(d_ff_11_q), .clk(and_4_out), .Q(d_ff_15_q));  // open: Qn, preset, reset
  D_Flip_Flop d_ff_16 (.D(d_ff_7_q), .clk(clock_1_out), .Q(d_ff_16_q));  // open: Qn, preset, reset
  D_Flip_Flop d_ff_17 (.D(d_ff_16_q), .clk(clock_1_out), .Q(d_ff_17_q));  // open: Qn, preset, reset
  D_Flip_Flop d_ff_18 (.D(d_ff_12_q), .clk(and_1_out), .Q(d_ff_18_q));  // open: Qn, preset, reset
  D_Flip_Flop d_ff_19 (.D(d_ff_13_q), .clk(and_2_out), .Q(d_ff_19_q));  // open: Qn, preset, reset
  D_Flip_Flop d_ff_20 (.D(d_ff_14_q), .clk(and_3_out), .Q(d_ff_20_q));  // open: Qn, preset, reset
  D_Flip_Flop d_ff_21 (.D(d_ff_15_q), .clk(and_4_out), .Q(d_ff_21_q));  // open: Qn, preset, reset
  D_Flip_Flop d_ff_22 (.D(d_ff_17_q), .clk(clock_1_out), .Q(d_ff_22_q));  // open: Qn, preset, reset
  D_Flip_Flop d_ff_23 (.D(d_ff_18_q), .clk(and_1_out), .Q(d_ff_23_q));  // open: Qn, preset, reset
  D_Flip_Flop d_ff_24 (.D(d_ff_19_q), .clk(and_2_out), .Q(d_ff_24_q));  // open: Qn, preset, reset
  D_Flip_Flop d_ff_25 (.D(d_ff_20_q), .clk(and_3_out), .Q(d_ff_25_q));  // open: Qn, preset, reset
  D_Flip_Flop d_ff_26 (.D(d_ff_21_q), .clk(and_4_out), .Q(d_ff_26_q));  // open: Qn, preset, reset
  D_Flip_Flop d_ff_27 (.D(d_ff_22_q), .clk(clock_1_out), .Q(d_ff_27_q));  // open: Qn, preset, reset
  D_Flip_Flop d_ff_28 (.D(d_ff_23_q), .clk(and_1_out), .Q(d_ff_28_q));  // open: Qn, preset, reset
  D_Flip_Flop d_ff_29 (.D(d_ff_24_q), .clk(and_2_out), .Q(d_ff_29_q));  // open: Qn, preset, reset
  D_Flip_Flop d_ff_30 (.D(d_ff_25_q), .clk(and_3_out), .Q(d_ff_30_q));  // open: Qn, preset, reset
  D_Flip_Flop d_ff_31 (.D(d_ff_26_q), .clk(and_4_out), .Q(d_ff_31_q));  // open: Qn, preset, reset
  D_Flip_Flop d_ff_32 (.D(d_ff_28_q), .clk(and_1_out), .Q(d_ff_32_q));  // open: Qn, preset, reset
  D_Flip_Flop d_ff_33 (.D(d_ff_29_q), .clk(and_2_out), .Q(d_ff_33_q));  // open: Qn, preset, reset
  D_Flip_Flop d_ff_34 (.D(d_ff_30_q), .clk(and_3_out), .Q(d_ff_34_q));  // open: Qn, preset, reset
  D_Flip_Flop d_ff_35 (.D(d_ff_31_q), .clk(and_4_out), .Q(d_ff_35_q));  // open: Qn, preset, reset
  D_Flip_Flop d_ff_36 (.D(d_ff_27_q), .clk(clock_1_out), .Q(d_ff_36_q));  // open: Qn, preset, reset
  D_Flip_Flop d_ff_37 (.D(d_ff_32_q), .clk(and_1_out));  // open: Q, Qn, preset, reset
  D_Flip_Flop d_ff_38 (.D(d_ff_33_q), .clk(and_2_out));  // open: Q, Qn, preset, reset
  D_Flip_Flop d_ff_39 (.D(d_ff_34_q), .clk(and_3_out));  // open: Q, Qn, preset, reset
  D_Flip_Flop d_ff_40 (.D(d_ff_35_q), .clk(and_4_out));  // open: Q, Qn, preset, reset
endmodule

module shit_Register_74164 (
  input  D,
  input  EN,
  input  [1:0] Addr
);

  wire clock_1_out, decoder_1_out0, decoder_1_out1, decoder_1_out2, decoder_1_out3, n74164_1_pin13,
       n74164_2_pin8, n74164_2_pin13, n74164_3_pin8, n74164_3_pin13, n74164_4_pin8, n74164_4_pin13,
       n74164_5_pin8;

  Clock clock_1 (.out(clock_1_out));
  Decoder #(.select(2)) decoder_1 (
    .out0(decoder_1_out0), .out1(decoder_1_out1), .out2(decoder_1_out2), .out3(decoder_1_out3), .sel(Addr),
    .en(EN));
  _74164 u_74164_1 (
    .pin1(D), .pin2(EN), .pin13(n74164_1_pin13), .pin8(clock_1_out));  // open: pin3, pin4, pin5, pin6, pin12, pin11, pin10, pin9
  _74164 u_74164_2 (
    .pin1(EN), .pin2(n74164_1_pin13), .pin13(n74164_2_pin13), .pin8(n74164_2_pin8));  // open: pin3, pin4, pin5, pin6, pin12, pin11, pin10, pin9
  _74164 u_74164_3 (
    .pin1(EN), .pin2(n74164_2_pin13), .pin13(n74164_3_pin13), .pin8(n74164_3_pin8));  // open: pin3, pin4, pin5, pin6, pin12, pin11, pin10, pin9
  _74164 u_74164_4 (
    .pin1(EN), .pin2(n74164_3_pin13), .pin13(n74164_4_pin13), .pin8(n74164_4_pin8));  // open: pin3, pin4, pin5, pin6, pin12, pin11, pin10, pin9
  _74164 u_74164_5 (
    .pin1(EN), .pin2(n74164_4_pin13), .pin8(n74164_5_pin8));  // open: pin3, pin4, pin5, pin6, pin13, pin12, pin11, pin10, pin9
  and and_1 (n74164_2_pin8, decoder_1_out0, clock_1_out);
  and and_2 (n74164_3_pin8, decoder_1_out1, clock_1_out);
  and and_3 (n74164_4_pin8, decoder_1_out2, clock_1_out);
  and and_4 (n74164_5_pin8, decoder_1_out3, clock_1_out);
endmodule
