// Logisim project EX1_2.circ as structural Verilog: 5 circuits, main circuit half_Adder
module half_Adder (
  input  A,
  input  B,
  output S,
  output Cout
);

  xor xor_1 (S, A, B);
  and and_1 (Cout, A, B);
endmodule

module full_Adder (
  input  A,
  input  B,
  input  Cin,
  output Cout,
  output S
);

  wire half_adder_1_cout, half_adder_1_s, half_adder_2_cout;

  half_Adder half_adder_1 (.A(A), .B(B), .S(half_adder_1_s), .Cout(half_adder_1_cout));
  half_Adder half_adder_2 (.A(half_adder_1_s), .B(Cin), .S(S), .Cout(half_adder_2_cout));
  or or_1 (Cout, half_adder_1_cout, half_adder_2_cout);
endmodule

module add_sub_8bit (
  input  A7,
  input  A6,
  input  A5,
  input  A4,
  input  A3,
  input  A2,
  input  A1,
  input  A0,
  input  B7,
  input  B6,
  input  B5,
  input  B4,
  input  B3,
  input  B2,
  input  B1,
  input  B0,
  input  ADD_SUB,
  output S7,
  output S6,
  output S5,
  output S4,
  output S3,
  output S2,
  output S1,
  output S0,
  output OVERFLOW
);

  wire full_adder_1_cout, full_adder_2_cout, full_adder_3_cout, full_adder_4_cout, full_adder_5_cout,
       full_adder_6_cout, full_adder_7_cout, not_1_out, xor_1_out, xor_2_out, xor_3_out, xor_4_out,
       xor_5_out, xor_6_out, xor_7_out, xor_8_out, xor_9_out, xor_10_out;

  xor xor_1 (xor_1_out, ADD_SUB, B0);
  xor xor_2 (xor_2_out, ADD_SUB, B1);
  xor xor_3 (xor_3_out, ADD_SUB, B2);
  xor xor_4 (xor_4_out, ADD_SUB, B3);
  xor xor_5 (xor_5_out, ADD_SUB, B4);
  xor xor_6 (xor_6_out, ADD_SUB, B5);
  xor xor_7 (xor_7_out, ADD_SUB, B6);
  xor xor_8 (xor_8_out, ADD_SUB, B7);
  full_Adder full_adder_1 (.A(A0), .B(xor_1_out), .Cin(ADD_SUB), .Cout(full_adder_1_cout), .S(S0));
  full_Adder full_adder_2 (.A(A1), .B(xor_2_out), .Cin(full_adder_1_cout), .Cout(full_adder_2_cout), .S(S1));
  full_Adder full_adder_3 (.A(A2), .B(xor_3_out), .Cin(full_adder_2_cout), .Cout(full_adder_3_cout), .S(S2));
  full_Adder full_adder_4 (.A(A3), .B(xor_4_out), .Cin(full_adder_3_cout), .Cout(full_adder_4_cout), .S(S3));
  full_Adder full_adder_5 (.A(A4), .B(xor_5_out), .Cin(full_adder_4_cout), .Cout(full_adder_5_cout), .S(S4));
  full_Adder full_adder_6 (.A(A5), .B(xor_6_out), .Cin(full_adder_5_cout), .Cout(full_adder_6_cout), .S(S5));
  full_Adder full_adder_7 (.A(A6), .B(xor_7_out), .Cin(full_adder_6_cout), .Cout(full_adder_7_cout), .S(S6));
  full_Adder full_adder_8 (.A(A7), .B(xor_8_out), .Cin(full_adder_7_cout), .S(S7));  // open: Cout
  buf xor_9 (xor_9_out, B7);  // XOR_Gate
  xor xor_10 (xor_10_out, B7, S7);
  not not_1 (not_1_out, xor_9_out);
  and and_1 (OVERFLOW, not_1_out, xor_10_out);
endmodule

module add_sub_8bit_abst (
  input  A7,
  input  A6,
  input  A5,
  input  A4,
  input  A3,
  input  A2,
  input  A1,
  input  A0,
  input  ADD_SUB,
  input  B7,
  input  B6,
  input  B5,
  input  B4,
  input  B3,
  input  B2,
  input  B1,
  input  B0,
  output S7,
  output S6,
  output S5,
  output S4,
  output S3,
  output S2,
  output S1,
  output S0,
  output OVERFLOW
);

  add_sub_8bit add_sub_8bit_1 (
    .A7(A7), .A6(A6), .A5(A5), .A4(A4), .A3(A3), .A2(A2), .A1(A1), .A0(A0), .B7(B7), .B6(B6), .B5(B5),
    .B4(B4), .B3(B3), .B2(B2), .B1(B1), .B0(B0), .ADD_SUB(ADD_SUB), .S7(S7), .S6(S6), .S5(S5), .S4(S4),
    .S3(S3), .S2(S2), .S1(S1), .S0(S0), .OVERFLOW(OVERFLOW));
endmodule

module EX2 (
  input  ADD_SUB,
  input  [7:0] in_2,
  output [7:0] out_3,
  output [7:0] out_4
);

  wire clock_1_out;
  wire [7:0] A_q, W_q;

  Register A (.D(in_2), .Q(A_q), .clk(clock_1_out));  // open: en, clr
  Clock clock_1 (.out(clock_1_out));
  add_sub_8bit_abst add_sub_8bit_abst_1 (
    .A7(W_q[7]), .A6(W_q[6]), .A5(W_q[5]), .A4(W_q[4]), .A3(W_q[3]), .A2(W_q[2]), .A1(W_q[1]), .A0(W_q[0]),
    .ADD_SUB(ADD_SUB), .B7(A_q[7]), .B6(A_q[6]), .B5(A_q[5]), .B4(A_q[4]), .B3(A_q[3]), .B2(A_q[2]),
    .B1(A_q[1]), .B0(A_q[0]), .S7(out_3[7]), .S6(out_3[6]), .S5(out_3[5]), .S4(out_3[4]), .S3(out_3[3]),
    .S2(out_3[2]), .S1(out_3[1]), .S0(out_3[0]));  // open: OVERFLOW
  Register W (.D(out_3), .Q(W_q), .clk(clock_1_out));  // open: en, clr

  assign out_4 = in_2;
endmodule
