// Logisim project EX4.circ as structural Verilog: 10 circuits, main circuit XOR_8bit
module XOR_8bit (
  input  [7:0] A,
  input  [7:0] B,
  input  Enable,
  output [7:0] X
);

  wire xor_1_out, xor_2_out, xor_3_out, xor_4_out, xor_5_out, xor_6_out, xor_7_out, xor_8_out;

  xor xor_1 (xor_1_out, B[0], A[0]);
  xor xor_2 (xor_2_out, B[1], A[1]);
  xor xor_3 (xor_3_out, B[2], A[2]);
  xor xor_4 (xor_4_out, B[3], A[3]);
  xor xor_5 (xor_5_out, B[4], A[4]);
  xor xor_6 (xor_6_out, B[5], A[5]);
  xor xor_7 (xor_7_out, B[6], A[6]);
  xor xor_8 (xor_8_out, B[7], A[7]);
  and and_1 (X[0], Enable, xor_1_out);
  and and_2 (X[1], Enable, xor_2_out);
  and and_3 (X[2], Enable, xor_3_out);
  and and_4 (X[3], Enable, xor_4_out);
  and and_5 (X[4], Enable, xor_5_out);
  and and_6 (X[5], Enable, xor_6_out);
  and and_7 (X[6], Enable, xor_7_out);
  and and_8 (X[7], Enable, xor_8_out);
endmodule

module AND_8bit (
  input  [7:0] A,
  input  [7:0] B,
  input  Enable,
  output [7:0] X
);

  wire and_1_out, and_2_out, and_3_out, and_4_out, and_5_out, and_6_out, and_7_out, and_8_out;

  and and_1 (and_1_out, B[0], A[0]);
  and and_2 (and_2_out, B[1], A[1]);
  and and_3 (and_3_out, B[2], A[2]);
  and and_4 (and_4_out, B[3], A[3]);
  and and_5 (and_5_out, B[4], A[4]);
  and and_6 (and_6_out, B[5], A[5]);
  and and_7 (and_7_out, B[6], A[6]);
  and and_8 (and_8_out, B[7], A[7]);
  and and_9 (X[0], Enable, and_1_out);
  and and_10 (X[1], Enable, and_2_out);
  and and_11 (X[2], Enable, and_3_out);
  and and_12 (X[3], Enable, and_4_out);
  and and_13 (X[4], Enable, and_5_out);
  and and_14 (X[5], Enable, and_6_out);
  and and_15 (X[6], Enable, and_7_out);
  and and_16 (X[7], Enable, and_8_out);
endmodule

module OR_8bit (
  input  [7:0] A,
  input  [7:0] B,
  input  Enable,
  output [7:0] X
);

  wire or_1_out, or_2_out, or_3_out, or_4_out, or_5_out, or_6_out, or_7_out, or_8_out;

  or or_1 (or_1_out, B[0], A[0]);
  or or_2 (or_2_out, B[1], A[1]);
  or or_3 (or_3_out, B[2], A[2]);
  or or_4 (or_4_out, B[3], A[3]);
  or or_5 (or_5_out, B[4], A[4]);
  or or_6 (or_6_out, B[5], A[5]);
  or or_7 (or_7_out, B[6], A[6]);
  or or_8 (or_8_out, B[7], A[7]);
  and and_1 (X[0], Enable, or_1_out);
  and and_2 (X[1], Enable, or_2_out);
  and and_3 (X[2], Enable, or_3_out);
  and and_4 (X[3], Enable, or_4_out);
  and and_5 (X[4], Enable, or_5_out);
  and and_6 (X[5], Enable, or_6_out);
  and and_7 (X[6], Enable, or_7_out);
  and and_8 (X[7], Enable, or_8_out);
endmodule

module INVERTER_8bit (
  input  [7:0] A,
  input  Enable,
  output [7:0] X
);

  wire not_1_out, not_2_out, not_3_out, not_4_out, not_5_out, not_6_out, not_7_out, not_8_out;

  not not_1 (not_1_out, A[0]);
  not not_2 (not_2_out, A[1]);
  not not_3 (not_3_out, A[2]);
  not not_4 (not_4_out, A[3]);
  not not_5 (not_5_out, A[4]);
  not not_6 (not_6_out, A[5]);
  not not_7 (not_7_out, A[6]);
  not not_8 (not_8_out, A[7]);
  and and_1 (X[0], Enable, not_1_out);
  and and_2 (X[1], Enable, not_2_out);
  and and_3 (X[2], Enable, not_3_out);
  and and_4 (X[3], Enable, not_4_out);
  and and_5 (X[4], Enable, not_5_out);
  and and_6 (X[5], Enable, not_6_out);
  and and_7 (X[6], Enable, not_7_out);
  and and_8 (X[7], Enable, not_8_out);
endmodule

module NAND_8bit (
  input  [7:0] A,
  input  [7:0] B,
  input  Enable,
  output [7:0] X
);

  wire nand_1_out, nand_2_out, nand_3_out, nand_4_out, nand_5_out, nand_6_out, nand_7_out, nand_8_out;

  nand nand_1 (nand_1_out, B[0], A[0]);
  nand nand_2 (nand_2_out, B[1], A[1]);
  nand nand_3 (nand_3_out, B[2], A[2]);
  nand nand_4 (nand_4_out, B[3], A[3]);
  nand nand_5 (nand_5_out, B[4], A[4]);
  nand nand_6 (nand_6_out, B[5], A[5]);
  nand nand_7 (nand_7_out, B[6], A[6]);
  nand nand_8 (nand_8_out, B[7], A[7]);
  and and_1 (X[0], Enable, nand_1_out);
  and and_2 (X[1], Enable, nand_2_out);
  and and_3 (X[2], Enable, nand_3_out);
  and and_4 (X[3], Enable, nand_4_out);
  and and_5 (X[4], Enable, nand_5_out);
  and and_6 (X[5], Enable, nand_6_out);
  and and_7 (X[6], Enable, nand_7_out);
  and and_8 (X[7], Enable, nand_8_out);
endmodule

module NOR_8bit (
  input  [7:0] A,
  input  [7:0] B,
  input  Enable,
  output [7:0] X
);

  wire nor_1_out, nor_2_out, nor_3_out, nor_4_out, nor_5_out, nor_6_out, nor_7_out, nor_8_out;

  nor nor_1 (nor_1_out, B[0], A[0]);
  nor nor_2 (nor_2_out, B[1], A[1]);
  nor nor_3 (nor_3_out, B[2], A[2]);
  nor nor_4 (nor_4_out, B[3], A[3]);
  nor nor_5 (nor_5_out, B[4], A[4]);
  nor nor_6 (nor_6_out, B[5], A[5]);
  nor nor_7 (nor_7_out, B[6], A[6]);
  nor nor_8 (nor_8_out, B[7], A[7]);
  and and_1 (X[0], Enable, nor_1_out);
  and and_2 (X[1], Enable, nor_2_out);
  and and_3 (X[2], Enable, nor_3_out);
  and and_4 (X[3], Enable, nor_4_out);
  and and_5 (X[4], Enable, nor_5_out);
  and and_6 (X[5], Enable, nor_6_out);
  and and_7 (X[6], Enable, nor_7_out);
  and and_8 (X[7], Enable, nor_8_out);
endmodule

module ADDER_8bit (
  input  [7:0] A,
  input  [7:0] B,
  input  Enable,
  output [7:0] X
);

  wire adder_1_cout, adder_1_out, adder_2_cout, adder_2_out, adder_3_cout, adder_3_out, adder_4_cout,
       adder_4_out, adder_5_cout, adder_5_out, adder_6_cout, adder_6_out, adder_7_cout, adder_7_out,
       adder_8_out;

  Adder #(.width(1)) adder_1 (.a(B[0]), .b(A[0]), .out(adder_1_out), .cin(1'b0), .cout(adder_1_cout));
  Adder #(.width(1)) adder_2 (.a(B[1]), .b(A[1]), .out(adder_2_out), .cin(adder_1_cout), .cout(adder_2_cout));
  Adder #(.width(1)) adder_3 (.a(B[2]), .b(A[2]), .out(adder_3_out), .cin(adder_2_cout), .cout(adder_3_cout));
  Adder #(.width(1)) adder_4 (.a(B[3]), .b(A[3]), .out(adder_4_out), .cin(adder_3_cout), .cout(adder_4_cout));
  Adder #(.width(1)) adder_5 (.a(B[4]), .b(A[4]), .out(adder_5_out), .cin(adder_4_cout), .cout(adder_5_cout));
  Adder #(.width(1)) adder_6 (.a(B[5]), .b(A[5]), .out(adder_6_out), .cin(adder_5_cout), .cout(adder_6_cout));
  Adder #(.width(1)) adder_7 (.a(B[6]), .b(A[6]), .out(adder_7_out), .cin(adder_6_cout), .cout(adder_7_cout));
  Adder #(.width(1)) adder_8 (.a(B[7]), .b(A[7]), .out(adder_8_out), .cin(adder_7_cout));  // open: cout
  and and_1 (X[0], Enable, adder_1_out);
  and and_2 (X[1], Enable, adder_2_out);
  and and_3 (X[2], Enable, adder_3_out);
  and and_4 (X[3], Enable, adder_4_out);
  and and_5 (X[4], Enable, adder_5_out);
  and and_6 (X[5], Enable, adder_6_out);
  and and_7 (X[6], Enable, adder_7_out);
  and and_8 (X[7], Enable, adder_8_out);
endmodule

module SUBTRACTOR_8bit (
  input  [7:0] A,
  input  [7:0] B,
  input  Enable,
  output [7:0] X
);

  wire adder_1_cout, adder_1_out, adder_2_cout, adder_2_out, adder_3_cout, adder_3_out, adder_4_cout,
       adder_4_out, adder_5_cout, adder_5_out, adder_6_cout, adder_6_out, adder_7_cout, adder_7_out,
       adder_8_out, not_1_out, not_2_out, not_3_out, not_4_out, not_5_out, not_6_out, not_7_out, not_8_out;

  not not_1 (not_1_out, B[0]);
  Adder #(.width(1)) adder_1 (.a(not_1_out), .b(A[0]), .out(adder_1_out), .cin(1'b1), .cout(adder_1_cout));
  not not_2 (not_2_out, B[1]);
  Adder #(.width(1)) adder_2 (.a(not_2_out), .b(A[1]), .out(adder_2_out), .cin(adder_1_cout), .cout(adder_2_cout));
  not not_3 (not_3_out, B[2]);
  Adder #(.width(1)) adder_3 (.a(not_3_out), .b(A[2]), .out(adder_3_out), .cin(adder_2_cout), .cout(adder_3_cout));
  not not_4 (not_4_out, B[3]);
  Adder #(.width(1)) adder_4 (.a(not_4_out), .b(A[3]), .out(adder_4_out), .cin(adder_3_cout), .cout(adder_4_cout));
  not not_5 (not_5_out, B[4]);
  Adder #(.width(1)) adder_5 (.a(not_5_out), .b(A[4]), .out(adder_5_out), .cin(adder_4_cout), .cout(adder_5_cout));
  not not_6 (not_6_out, B[5]);
  Adder #(.width(1)) adder_6 (.a(not_6_out), .b(A[5]), .out(adder_6_out), .cin(adder_5_cout), .cout(adder_6_cout));
  not not_7 (not_7_out, B[6]);
  Adder #(.width(1)) adder_7 (.a(not_7_out), .b(A[6]), .out(adder_7_out), .cin(adder_6_cout), .cout(adder_7_cout));
  not not_8 (not_8_out, B[7]);
  Adder #(.width(1)) adder_8 (.a(not_8_out), .b(A[7]), .out(adder_8_out), .cin(adder_7_cout));  // open: cout
  and and_1 (X[0], Enable, adder_1_out);
  and and_2 (X[1], Enable, adder_2_out);
  and and_3 (X[2], Enable, adder_3_out);
  and and_4 (X[3], Enable, adder_4_out);
  and and_5 (X[4], Enable, adder_5_out);
  and and_6 (X[5], Enable, adder_6_out);
  and and_7 (X[6], Enable, adder_7_out);
  and and_8 (X[7], Enable, adder_8_out);
endmodule

module ULA (
  input  [7:0] A,
  input  [7:0] B,
  input  [2:0] S,
  output [7:0] X
);

  wire demultiplexer_1_out0, demultiplexer_1_out1, demultiplexer_1_out2, demultiplexer_1_out3,
       demultiplexer_1_out4, demultiplexer_1_out5, demultiplexer_1_out6, demultiplexer_1_out7;
  wire [7:0] adder_8bit_1_x, and_8bit_1_x, inverter_8bit_1_x, nand_8bit_1_x, nor_8bit_1_x, or_8bit_1_x,
       subtractor_8bit_1_x, xor_8bit_1_x;

  Demultiplexer #(.select(3)) demultiplexer_1 (
    .out0(demultiplexer_1_out0), .out1(demultiplexer_1_out1), .out2(demultiplexer_1_out2),
    .out3(demultiplexer_1_out3), .out4(demultiplexer_1_out4), .out5(demultiplexer_1_out5),
    .out6(demultiplexer_1_out6), .out7(demultiplexer_1_out7), .in(1'b1), .sel(S));
  XOR_8bit xor_8bit_1 (.A(A), .B(B), .Enable(demultiplexer_1_out0), .X(xor_8bit_1_x));
  AND_8bit and_8bit_1 (.A(A), .B(B), .Enable(demultiplexer_1_out1), .X(and_8bit_1_x));
  OR_8bit or_8bit_1 (.A(A), .B(B), .Enable(demultiplexer_1_out2), .X(or_8bit_1_x));
  INVERTER_8bit inverter_8bit_1 (.A(A), .Enable(demultiplexer_1_out3), .X(inverter_8bit_1_x));
  NAND_8bit nand_8bit_1 (.A(A), .B(B), .Enable(demultiplexer_1_out4), .X(nand_8bit_1_x));
  NOR_8bit nor_8bit_1 (.A(A), .B(B), .Enable(demultiplexer_1_out5), .X(nor_8bit_1_x));
  ADDER_8bit adder_8bit_1 (.A(A), .B(B), .Enable(demultiplexer_1_out6), .X(adder_8bit_1_x));
  SUBTRACTOR_8bit subtractor_8bit_1 (.A(A), .B(B), .Enable(demultiplexer_1_out7), .X(subtractor_8bit_1_x));
  Multiplexer #(.select(3), .width(8)) multiplexer_1 (
    .in0(xor_8bit_1_x), .in1(and_8bit_1_x), .in2(or_8bit_1_x), .in3(inverter_8bit_1_x), .in4(nand_8bit_1_x),
    .in5(nor_8bit_1_x), .in6(adder_8bit_1_x), .in7(subtractor_8bit_1_x), .out(X), .sel(S));
endmodule

module ULA_AW (
  input  [7:0] Data,
  input  Enable,
  input  [2:0] S
);

  wire clock_1_out;
  wire [7:0] A_q, ula_1_x, W_q;

  Clock clock_1 (.out(clock_1_out));
  Register A (.D(Data), .en(Enable), .clk(clock_1_out), .Q(A_q));  // open: clr
  ULA ula_1 (.A(W_q), .B(A_q), .S(S), .X(ula_1_x));
  Register W (.D(ula_1_x), .en(Enable), .clk(clock_1_out), .Q(W_q));  // open: clr
endmodule
